# Fritzing sketch mp3_audio_signal_photo_registor (saved by Fritzing 0.8.7b)
breadboards: 1

parts:
  Part1 = Arduino Mega 2560 (Rev3)
  IC1 = IC, DIP package, 14 pins [chip_label=LM324]
  SPKR1 = Loudspeaker
  R1 = Rotary Potentiometer (Small) [maximum_resistance=100kΩ package=THT]
  R2 = Resistor [tolerance=±5% resistance=47 package=THT]
  C1 = Electrolytic Capacitor [capacitance=10µF package="100 mil [THT, electrolytic]"]
  R3 = Resistor [tolerance=±5% resistance=10k package=THT]
  LED1 = LED - 5mm [color="Red (633nm)" package="5 mm [THT]"]
  R4 = Resistor [tolerance=±5% resistance=220 package=THT]
  R5 = PHOTOCELL [package=photocell-kit]
  R6 = PHOTOCELL [package=photocell-kit]
  LED2 = LED - 5mm [color="Red (633nm)" package="5 mm [THT]"]
  R7 = Resistor [tolerance=±5% resistance=10k package=THT]
  R8 = Resistor [tolerance=±5% resistance=10k package=THT]
  R9 = Resistor [tolerance=±5% resistance=220 package=THT]

nets:
  N1: Part1.A0, R5.P$1
  N2: Part1.A1, R6.P$1
  N3: Part1.5V, R7.Pin_1
  N4: Part1.GND, IC1.pin11, SPKR1.pin1, R9.Pin_0
  N5: Part1.D7_PWM, LED2.anode
  N6: IC1.pin1, IC1.pin5
  N7: IC1.pin3, SPKR1.pin2
  N8: IC1.pin4, R8.Pin_1
  N9: IC1.pin6, IC1.pin7, C1.-, R3.Pin_0, LED1.cathode
  N10: R1.leg1, R2.Pin_0
  N11: R2.Pin_1, C1.+, R3.Pin_1, R4.Pin_1
  N12: LED1.anode, R4.Pin_0
  N13: R5.P$2, R8.Pin_0
  N14: R6.P$2, R7.Pin_0
  N15: LED2.cathode, R9.Pin_1

notes:
  eutotong dic speaker + and -
