# Fritzing sketch _02_lcd_2x16_distance_sensor (saved by Fritzing 0.8.7b)
breadboards: 1

parts:
  Part1 = Arduino Mega 2560 (Rev3)
  LCD1 = LCD screen
  R1 = Resistor [tolerance=±5% resistance=2.2k package=THT]
  R2 = Resistor [tolerance=±5% resistance=220 package=THT]

nets:
  N1: Part1.D12_PWM, LCD1.RS
  N2: Part1.D11_PWM, LCD1.E
  5V: Part1.5V, LCD1.VDD, R2.Pin_1
  GND: Part1.GND, LCD1.VSS, LCD1.R/W, LCD1.LED-, R1.Pin_0
  N3: Part1.D2_PWM, LCD1.DB7
  N4: Part1.D3_PWM, LCD1.DB6
  N5: Part1.D4_PWM, LCD1.DB5
  N6: Part1.D5_PWM, LCD1.DB4
  N7: LCD1.V0, R1.Pin_1
  N8: LCD1.LED+, R2.Pin_0

notes:
  HC-SR04
  pin7 connect to trig and pin6 connect to echo on HC-SR04
